# Fritzing sketch RFCardPay (saved by Fritzing 0.9.2b)
breadboards: 1

parts:
  Part1 = Arduino Mega 2560 (Rev3)
  Part2 = RFID-RC522-v3
  Mod1 = OLED Mono 0.56 inch blue or white
  Part3 = Bluetooth HC-06
  S1 = Pushbutton [package="[THT]"]
  S2 = Pushbutton [package="[THT]"]
  S3 = Pushbutton [package="[THT]"]

nets:
  N1: Part1.D21/SCL, Mod1.SCL
  N2: Part1.D20/SDA, Mod1.SDA
  N3: Part1.D15/RX3, Part3.TXD
  N4: Part1.D14/TX3, Part3.RXD
  VCC: Part1.5V, Part2.3.3V, Mod1.VCC, Part3.VCC
  GND: Part1.GND, Part2.GND, Mod1.GND, Part3.GND, S1.Pin_1, S1.Pin_2, S2.Pin_2, S3.Pin_1, S3.Pin_2
  N5: Part1.D5_PWM, Part2.RST
  N6: Part1.D23, S1.Pin_3, S1.Pin_4
  N7: Part1.D25, S2.Pin_3, S2.Pin_4
  N8: Part1.D39, S3.Pin_3, S3.Pin_4
  N9: Part1.D50, Part2.MISO
  N10: Part1.D51, Part2.MOSI
  N11: Part1.D52, Part2.SCK
  N12: Part1.D53, Part2.SDA

custom parts:
  RFID-RC522-v3: A simple China made RFID-RC522 Reader (6x4 cm); do check the pin labels, as this is a MFRC522 based clone.
  OLED Mono 0.56 inch blue or white: OLED, I2C 3.3V - 5V Blue and White text versions
